# Fritzing sketch hello-led (saved by Fritzing 1.0.2b)
breadboards: 1

parts:
  LED1 = LED - 5mm [color="Red (660nm)" current=30mA package="5 mm [THT]"]
  R1 = Resistor [tolerance=±5% power=0.25W resistance=220 package=THT]
  WeMos_D1_Mini1 = WeMos D1 Mini

nets:
  N1: LED1.cathode, R1.Pin_0
  N2: LED1.anode, WeMos_D1_Mini1.5V
  N3: R1.Pin_1, WeMos_D1_Mini1.G

custom parts:
  WeMos D1 Mini: The D1 mini is a mini wifi board based on ESP-8266EX.
