# Fritzing sketch temp-and-humidity (saved by Fritzing 1.0.2b)
breadboards: 1

parts:
  LED1 = LED - 5mm [color="Red (660nm)" current=30mA package="5 mm [THT]"]
  R1 = Resistor [tolerance=±5% power=0.25W resistance=220 package=THT]
  WeMos_D1_Mini1 = WeMos D1 Mini
  S1 = Pushbutton [package="[THT]"]
  Mod1 = KY-015 Temperature & Humidity Sensor Module [package="Breakout board"]

nets:
  N1: LED1.cathode, R1.Pin_0
  N2: LED1.anode, WeMos_D1_Mini1.D1
  N3: R1.Pin_1, WeMos_D1_Mini1.G, S1.Pin_1, S1.Pin_2, Mod1.-
  N4: WeMos_D1_Mini1.5V, Mod1.S
  N5: WeMos_D1_Mini1.D5, S1.Pin_3, S1.Pin_4
  N6: WeMos_D1_Mini1.D6, Mod1.Vin

notes:
  DHT11, DHT22 AM2303 or KY-015
  Check data sheet or board prints for connection details

custom parts:
  WeMos D1 Mini: The D1 mini is a mini wifi board based on ESP-8266EX.
  KY-015 Temperature & Humidity Sensor Module: KY-015 temperature and humidity sensor module, provides a low-latency serial interface to measure humidity and temperature.
